# Fritzing sketch Riego_2.0 (saved by Fritzing 0.9.4)

parts:
  PiZero1 = Raspberry Pi Zero
  Componente1 = Adafruit ADS1115 16Bit I2C ADC [part_number="Adafruit #1085"]
  U1 = 4-Channel 5v Relay Shield [package=relay-4ch5v10a]
  JACK1 = 2.1mm Barrel Jack with Terminal Block
  JACK2 = 2.1mm Barrel Jack with Terminal Block
  2_Channel_Relay1 = 2 Channel Power Relay
  Componente2 = FC-28 Soil Hygrometer Module - Probe
  YL-83_-_Control_Board1 = YL-83 Rain Sensor - Control Board
  Water_Level_Sensor1 = Water Level Sensor
  U2 = Voltage Regulator [package=sot223]
  Componente3 = FC-28 Soil Hygrometer Module - Probe
  YL-83_-_Control_Board2 = YL-83 Rain Sensor - Control Board
  Componente4 = FC-28 Soil Hygrometer Module - Probe
  YL-83_-_Control_Board3 = YL-83 Rain Sensor - Control Board
  KY-1 = Keyes Relay [package=THT]
  M1 = DC Motor
  VALVE1 = Plastic Solenoid Valve

nets:
  N1: PiZero1.5v, JACK1.POS, U2.IN, KY-1.C
  N2: Componente1.AIN3, YL-83_-_Control_Board3.AO
  N3: Componente1.AIN2, YL-83_-_Control_Board2.AO
  N4: Componente1.AIN1, YL-83_-_Control_Board1.AO
  N5: Componente1.AIN0, Water_Level_Sensor1.SIG
  GND: Componente1.GND, YL-83_-_Control_Board1.GND, Water_Level_Sensor1.GND, YL-83_-_Control_Board2.GND, YL-83_-_Control_Board3.GND
  N6: Componente1.VDD, 2_Channel_Relay1.K1-NO
  N7: U1.K1-Off, U1.K2-Off, U1.K3-Off, U1.K4-Off, JACK2.POS
  N8: U1.K1-On, VALVE1.no_name_yet
  N9: JACK1.NEG, M1.pin_1
  N10: 2_Channel_Relay1.K1-COM, 2_Channel_Relay1.K2-COM, U2.OUT
  VCC: 2_Channel_Relay1.K2-NO, YL-83_-_Control_Board1.VCC, Water_Level_Sensor1.VCC, YL-83_-_Control_Board2.VCC, YL-83_-_Control_Board3.VCC
  N11: Componente2.POS, YL-83_-_Control_Board1.POS
  N12: Componente2.NEG, YL-83_-_Control_Board1.NEG
  N13: Componente3.POS, YL-83_-_Control_Board2.POS
  N14: Componente3.NEG, YL-83_-_Control_Board2.NEG
  N15: Componente4.POS, YL-83_-_Control_Board3.POS
  N16: Componente4.NEG, YL-83_-_Control_Board3.NEG

notes:
  5V
  12V
  3.3V

custom parts:
  Adafruit ADS1115 16Bit I2C ADC: For microcontrollers without an analog-to-digital converter or when you want a higher-precision ADC, the ADS1115 provides 16-bit precision at 860 samples/second over I2C. The chip can be configured as 4 single-ended input channels, or two differential channels. As a nice bonus, it even includes a programmable gain amplifier, up to x16, to help boost up smaller single/differential signals to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
  4-Channel 5v Relay Shield: 4 Channel 5v Relay Shield w. 2x SPD-06VDC-SD-C
  2 Channel Power Relay: A 2 channel power relay. The module operates at 5V.
  FC-28 Soil Hygrometer Module - Probe: The FC-28 is a soil hygrometer module that uses the Texas Instruments LM393 comparator chip to provide an analog measurement of soil humidity.
  YL-83 Rain Sensor - Control Board: The YL-83 is a rain sensor that has more resistance when dry and less resistance when wet. The module runs at 5V.
  Water Level Sensor: A water level sensor. This sensor operates at 3V to 5V. The Sig (signal) pin outputs an analogue signal that is in proportion to the amount of water in contact with the sensor.
  Keyes Relay: The Keyes 5V relay module is suitable for SCM development, home appliance control. It uses a 5V~12V TIL control signal which can control DC / AC signal.
