# Fritzing sketch RpiZ_bme280 (saved by Fritzing 0.9.4)

parts:
  PiZero1 = Raspberry Pi Zero
  BMP280_Breakout1 = BMP280 Breakout Board [part_number=BMP280]

nets:
  3.3V: PiZero1.3.3v, BMP280_Breakout1.VCC
  N1: PiZero1.GPIO2_(SDA1), BMP280_Breakout1.SDA
  N2: PiZero1.GPIO3_(SCL), BMP280_Breakout1.SCL
  N3: PiZero1.Ground, BMP280_Breakout1.GND

custom parts:
  BMP280 Breakout Board: This is a breakout board for the Bosch Sensortec BMP280, "an absolute barometric pressure sensor especially designed for mobile applications." The operation range is 300 to 1100 hPa. Supply voltage is 1.2 to 3.6V. Operating temperature range is -40 to +85 °C.
